# Fritzing sketch MontageGarageV2 (1) (saved by Fritzing 0.9.9b)
breadboards: 2

parts:
  U1 = NodeMCU V1.0
  KY-1 = Keyes Relay [package=THT]
  KY-2 = Keyes Relay [package=THT]
  HC-SR04_Sensor_1 = HC-SR04 Ultrasonic Distance Sensor

nets:
  N1: U1.D1, HC-SR04_Sensor_1.TRIG
  N2: U1.D2, HC-SR04_Sensor_1.ECHO
  N3: U1.GND, KY-2.ground
  N4: U1.D7, KY-1.signal
  N5: U1.D8, KY-2.signal
  N6: KY-1.power, KY-2.power, HC-SR04_Sensor_1.VCC
  N7: KY-1.ground, HC-SR04_Sensor_1.GND

notes:
  Pin 10 Garage
  Pin 11 Garage
  Pin 3 ou 5 Garage

custom parts:
  NodeMCU V1.0: ESP8266 based NodeMCU
  Keyes Relay: The Keyes 5V relay module is suitable for SCM development, home appliance control. It uses a 5V~12V TIL control signal which can control DC / AC signal.
